// Digital circuit part_c.dig as structural Verilog
module part_c (
  input  in_0,
  input  in_1,
  input  in_2,
  output out_0
);

  wire nfet_4_s, nfet_5_s, nfet_6_s, nfet_7_s, nfet_8_s, nfet_9_s, nfet_10_s, nfet_11_s, nfet_12_s,
       nfet_13_s, nfet_14_s, nfet_15_s, nfet_16_s, nfet_17_s, nfet_18_s, pfet_1_d, pfet_2_d, pfet_3_d,
       pfet_19_d, pfet_20_d, pfet_21_d, pfet_22_d;

  PFET pfet_1 (.G(in_0), .S(1'b1), .D(pfet_1_d));
  NFET nfet_1 (.G(in_0), .D(pfet_1_d), .S(1'b0));
  PFET pfet_2 (.G(in_1), .S(1'b1), .D(pfet_2_d));
  NFET nfet_2 (.G(in_1), .D(pfet_2_d), .S(1'b0));
  PFET pfet_3 (.G(in_2), .S(1'b1), .D(pfet_3_d));
  NFET nfet_3 (.G(in_2), .D(pfet_3_d), .S(1'b0));
  NFET nfet_4 (.G(pfet_1_d), .D(1'b1), .S(nfet_4_s));
  NFET nfet_5 (.G(pfet_2_d), .D(nfet_4_s), .S(nfet_5_s));
  NFET nfet_6 (.G(pfet_3_d), .D(nfet_5_s), .S(nfet_6_s));
  PFET pfet_4 (.G(pfet_3_d), .S(nfet_6_s), .D(1'b0));
  NFET nfet_7 (.G(pfet_1_d), .D(1'b1), .S(nfet_7_s));
  NFET nfet_8 (.G(in_1), .D(nfet_7_s), .S(nfet_8_s));
  NFET nfet_9 (.G(pfet_3_d), .D(nfet_8_s), .S(nfet_9_s));
  PFET pfet_5 (.G(pfet_3_d), .S(nfet_9_s), .D(1'b0));
  NFET nfet_10 (.G(in_0), .D(1'b1), .S(nfet_10_s));
  NFET nfet_11 (.G(pfet_2_d), .D(nfet_10_s), .S(nfet_11_s));
  NFET nfet_12 (.G(pfet_3_d), .D(nfet_11_s), .S(nfet_12_s));
  PFET pfet_6 (.G(pfet_3_d), .S(nfet_12_s), .D(1'b0));
  PFET pfet_7 (.G(pfet_2_d), .S(nfet_6_s), .D(1'b0));
  PFET pfet_8 (.G(in_1), .S(nfet_9_s), .D(1'b0));
  PFET pfet_9 (.G(pfet_2_d), .S(nfet_12_s), .D(1'b0));
  NFET nfet_13 (.G(in_0), .D(1'b1), .S(nfet_13_s));
  NFET nfet_14 (.G(pfet_2_d), .D(nfet_13_s), .S(nfet_14_s));
  NFET nfet_15 (.G(in_2), .D(nfet_14_s), .S(nfet_15_s));
  PFET pfet_10 (.G(in_2), .S(nfet_15_s), .D(1'b0));
  NFET nfet_16 (.G(in_0), .D(1'b1), .S(nfet_16_s));
  NFET nfet_17 (.G(in_1), .D(nfet_16_s), .S(nfet_17_s));
  NFET nfet_18 (.G(in_2), .D(nfet_17_s), .S(nfet_18_s));
  PFET pfet_11 (.G(in_2), .S(nfet_18_s), .D(1'b0));
  PFET pfet_12 (.G(pfet_1_d), .S(nfet_6_s), .D(1'b0));
  PFET pfet_13 (.G(pfet_1_d), .S(nfet_9_s), .D(1'b0));
  PFET pfet_14 (.G(pfet_2_d), .S(nfet_15_s), .D(1'b0));
  PFET pfet_15 (.G(in_1), .S(nfet_18_s), .D(1'b0));
  PFET pfet_16 (.G(in_0), .S(nfet_12_s), .D(1'b0));
  PFET pfet_17 (.G(in_0), .S(nfet_15_s), .D(1'b0));
  PFET pfet_18 (.G(in_0), .S(nfet_18_s), .D(1'b0));
  NFET nfet_19 (.G(nfet_6_s), .D(1'b1), .S(out_0));
  PFET pfet_19 (.G(nfet_12_s), .S(out_0), .D(pfet_19_d));
  PFET pfet_20 (.G(nfet_9_s), .S(pfet_19_d), .D(pfet_20_d));
  PFET pfet_21 (.G(nfet_6_s), .S(pfet_20_d), .D(pfet_21_d));
  PFET pfet_22 (.G(nfet_15_s), .S(pfet_21_d), .D(pfet_22_d));
  PFET pfet_23 (.G(nfet_18_s), .S(pfet_22_d), .D(1'b0));
  NFET nfet_20 (.G(nfet_9_s), .D(1'b1), .S(out_0));
  NFET nfet_21 (.G(nfet_12_s), .D(1'b1), .S(out_0));
  NFET nfet_22 (.G(nfet_15_s), .D(1'b1), .S(out_0));
  NFET nfet_23 (.G(nfet_18_s), .D(1'b1), .S(out_0));
endmodule

/* Test case part_c_test:
in_0 in_1 in_2 out_0
0 0 0 1
0 0 1 0
0 1 0 1
0 1 1 0
1 0 0 1
1 0 1 1
1 1 0 0
1 1 1 1
*/
